# Fritzing sketch NodeMCU V3 (saved by Fritzing 0.9.3b)
breadboards: 1

parts:
  U1 = NodeMCU V3.0
  DHT1 = DHT11 Humitidy and Temperature Sensor (3 pins)
  Mod1 = KY-026 Flame Sensor Module [package="Breakout board"]
  J1 = Piezo Speaker
  LCD1 = TFT 1.8 inch 160x128 w SD
  MQ-2 = MQ-7 breakout

nets:
  N1: U1.D0, LCD1.pin_7
  N2: U1.D1, LCD1.pin3
  N3: U1.D2, LCD1.pin_6
  N4: U1.D3, LCD1.pin4
  N5: U1.3V3, LCD1.pin_8
  GND: U1.GND, DHT1.GND, Mod1.G, J1.pin1, LCD1.pin2, MQ-2.GND
  N6: U1.D5, LCD1.pin_5
  N7: U1.D6, DHT1.DATA
  N8: U1.D7, Mod1.D0
  N9: U1.D8, J1.pin2
  VIN: U1.Vin, DHT1.VDD, Mod1.+, LCD1.pin_1, MQ-2.VCC
  N10: U1.A0, MQ-2.AO

custom parts:
  NodeMCU V3.0: NodeMcu V3 Lua WIFI Development Board
  DHT11 Humitidy and Temperature Sensor (3 pins): DHT11 Humidity and Temperature Sensor (3 pins) from the design created by John De Cristofaro for Adafruit Industries.
  KY-026 Flame Sensor Module: KY-026 Flame Sensor Module reacts in the presence of fire.
  TFT 1.8 inch 160x128 w SD: This is a generic 1.8 tft spi lcd display available on ebay and others. The 1.8" display has 128x160 color pixels.
  MQ-7 breakout: SKU: 101282
